# Fritzing sketch Hello_FunctionsFritzing (saved by Fritzing 0.9.3b)
breadboards: 1

parts:
  Part1 = Arduino Uno (Rev3) - ICSP
  HC-SR04_Sensor_1 = HC-SR04 Ultrasonic Distance Sensor
  J1 = Basic Servo

nets:
  GND: Part1.GND, HC-SR04_Sensor_1.GND, J1.gnd
  N1: Part1.D2, HC-SR04_Sensor_1.ECHO
  N2: Part1.D3_PWM, HC-SR04_Sensor_1.TRIG
  N3: Part1.D7, J1.pulse
  VCC: Part1.5V, HC-SR04_Sensor_1.VCC, J1.vcc
