# Fritzing sketch NewPing()Fritzing (saved by Fritzing 0.9.3b)
breadboards: 1

parts:
  Part2 = Arduino Uno (Rev3) - ICSP
  HC-SR04_Sensor_2 = HC-SR04 Ultrasonic Distance Sensor
  LED1 = LEDs [package=led10mm]

nets:
  N1: Part2.D9_PWM, LED1.C
  N2: Part2.D2, HC-SR04_Sensor_2.ECHO
  N3: Part2.D3_PWM, HC-SR04_Sensor_2.TRIG
  5V: Part2.5V, HC-SR04_Sensor_2.VCC
  GND: Part2.GND, HC-SR04_Sensor_2.GND, LED1.A
